// Logisim project Project3Given.circ as structural Verilog: 9 circuits, main circuit CPU15
module main (
  input  EnableBreakpoint,
  input  [14:0] Breakpoint
);

  wire and_2_out, and_3_out, chipset_1_irq, CLK, clock_1_out, cpu15_1_c, cpu15_1_e, cpu15_1_i, cpu15_1_n,
       cpu15_1_o, cpu15_1_z, KBCLR, KBIRQ, KBRD, MEMCS, nand_1_out, RE, TTYCLR, TTYWE, WE;
  wire [6:0] KBDATA, TTYDATA;
  wire [7:0] cpu15_1_srf;
  wire [14:0] ADDR, chipset_1_ivect, chipset_1_led0, chipset_1_led1, chipset_1_led2, chipset_1_led3,
       chipset_1_led4, chipset_1_led5, chipset_1_led6, chipset_1_led7, chipset_1_led8, chipset_1_led9,
       chipset_1_leda, chipset_1_ledb, chipset_1_ledc, chipset_1_ledd, chipset_1_lede, cpu15_1_ib,
       cpu15_1_pc, cpu15_1_r0, cpu15_1_r1, cpu15_1_r2, cpu15_1_r3, cpu15_1_r4, cpu15_1_r5, cpu15_1_r6,
       cpu15_1_r7, cpu15_1_srp, DATA, xnor_1_out;

  Clock clock_1 (.out(clock_1_out));
  nand nand_1 (nand_1_out, EnableBreakpoint, xnor_1_out[0], xnor_1_out[1], xnor_1_out[2], xnor_1_out[3], xnor_1_out[4], xnor_1_out[5], xnor_1_out[6], xnor_1_out[7], xnor_1_out[8], xnor_1_out[9], xnor_1_out[10], xnor_1_out[11], xnor_1_out[12], xnor_1_out[13], xnor_1_out[14], 1'b1);
  and and_1 (CLK, clock_1_out, nand_1_out);
  assign xnor_1_out = ~(Breakpoint ^ cpu15_1_pc);  // XNOR_Gate xnor_1, 15 bits wide
  LED I (.in(cpu15_1_i));
  LED Z (.in(cpu15_1_z));
  LED N (.in(cpu15_1_n));
  LED O (.in(cpu15_1_o));
  LED C (.in(cpu15_1_c));
  LED E (.in(cpu15_1_e));
  and and_2 (and_2_out, WE, MEMCS);
  and and_3 (and_3_out, MEMCS, RE);
  RAM #(.addrWidth(15), .asyncread("true"), .dataWidth(15), .databus("bidir")) ram_1 (
    .addr(ADDR), .we(and_2_out), .oe(and_3_out), .clk(CLK), .data(DATA));
  // Probe on cpu15_1_pc
  // Probe on cpu15_1_ib
  // Probe on cpu15_1_srp
  // Probe on cpu15_1_srf
  // Probe on cpu15_1_r0
  // Probe on cpu15_1_r1
  // Probe on cpu15_1_r2
  // Probe on cpu15_1_r3
  // Probe on cpu15_1_r4
  // Probe on cpu15_1_r5
  // Probe on cpu15_1_r6
  // Probe on cpu15_1_r7
  CPU15 cpu15_1 (
    .I(cpu15_1_i), .Z(cpu15_1_z), .N(cpu15_1_n), .O(cpu15_1_o), .C(cpu15_1_c), .E(cpu15_1_e),
    .PC(cpu15_1_pc), .IB(cpu15_1_ib), .SRP(cpu15_1_srp), .SRF(cpu15_1_srf), .R0(cpu15_1_r0), .R1(cpu15_1_r1),
    .R2(cpu15_1_r2), .R3(cpu15_1_r3), .R4(cpu15_1_r4), .R5(cpu15_1_r5), .R6(cpu15_1_r6), .R7(cpu15_1_r7),
    .CLK(CLK), .IRQ(chipset_1_irq), .RE(RE), .WE(WE), .ADDR(ADDR), .DATAIN(DATA), .DATAOUT(DATA));
  // Probe on ADDR
  // Probe on DATA
  // Probe on chipset_1_ivect
  // Probe on TTYDATA
  CHIPSET chipset_1 (
    .RE(RE), .WE(WE), .ADDR(ADDR), .CPUDATAIN(DATA), .CPUDATAOUT(DATA), .IRQ(chipset_1_irq),
    .IVECT(chipset_1_ivect), .CLK(CLK), .MEMCS(MEMCS), .TTYWR(TTYWE), .TTYCLR(TTYCLR), .TTYDATA(TTYDATA),
    .KBRD(KBRD), .KBCLR(KBCLR), .KBIRQ(KBIRQ), .KBDATA(KBDATA), .LED0(chipset_1_led0), .LED1(chipset_1_led1),
    .LED2(chipset_1_led2), .LED3(chipset_1_led3), .LED4(chipset_1_led4), .LED5(chipset_1_led5),
    .LED6(chipset_1_led6), .LED7(chipset_1_led7), .LED8(chipset_1_led8), .LED9(chipset_1_led9),
    .LEDA(chipset_1_leda), .LEDB(chipset_1_ledb), .LEDC(chipset_1_ledc), .LEDD(chipset_1_ledd),
    .LEDE(chipset_1_lede));
  TTY tty_1 (.data(TTYDATA), .clk(CLK), .we(TTYWE), .clr(TTYCLR));
  Keyboard keyboard_1 (.clk(CLK), .re(KBRD), .clr(KBCLR), .avail(KBIRQ), .data(KBDATA));
  DotMatrix #(.matrixcols(15), .matrixrows(15)) dotmatrix_1 (
    .col0(chipset_1_led0), .col1(chipset_1_led1), .col2(chipset_1_led2), .col3(chipset_1_led3),
    .col4(chipset_1_led4), .col5(chipset_1_led5), .col6(chipset_1_led6), .col7(chipset_1_led7),
    .col8(chipset_1_led8), .col9(chipset_1_led9), .col10(chipset_1_leda), .col11(chipset_1_ledb),
    .col12(chipset_1_ledc), .col13(chipset_1_ledd), .col14(chipset_1_lede));
endmodule

// CPU
module CPU15 (
  input  [14:0] DATAIN,
  input  CLK,
  input  IRQ,
  output [14:0] PC,
  output [14:0] IB,
  output [14:0] SRP,
  output [7:0] SRF,
  output [14:0] R0,
  output [14:0] R1,
  output [14:0] R2,
  output [14:0] R3,
  output [14:0] R4,
  output [14:0] R5,
  output [14:0] R6,
  output [14:0] R7,
  output RE,
  output WE,
  output I,
  output Z,
  output [14:0] ADDR,
  output N,
  output O,
  output C,
  output E,
  output [14:0] DATAOUT
);


  // Other names for the same wires on the sheet: DATA[14:0] = DATAIN
endmodule

module CHIPSET (
  input  RE,
  input  WE,
  input  [14:0] ADDR,
  input  [14:0] CPUDATAIN,
  input  KBIRQ,
  input  [6:0] KBDATA,
  input  CLK,
  output MEMCS,
  output TTYWR,
  output [14:0] IVECT,
  output TTYCLR,
  output [6:0] TTYDATA,
  output KBRD,
  output KBCLR,
  output [14:0] CPUDATAOUT,
  output IRQ,
  output [14:0] LED0,
  output [14:0] LED1,
  output [14:0] LED2,
  output [14:0] LED3,
  output [14:0] LED4,
  output [14:0] LED5,
  output [14:0] LED6,
  output [14:0] LED7,
  output [14:0] LED8,
  output [14:0] LED9,
  output [14:0] LEDA,
  output [14:0] LEDB,
  output [14:0] LEDC,
  output [14:0] LEDD,
  output [14:0] LEDE
);

  wire and_1_out, and_8_out, and_10_out, DATA7, IOCS, IVECTADDR, IVECTEN, IVECTRE, KBCS, LED0EN, LED0END,
       LED1EN, LED1END, LED2EN, LED2END, LED3EN, LED3END, LED4EN, LED4END, LED5EN, LED5END, LED6EN, LED6END,
       LED7EN, LED7END, LED8EN, LED8END, LED9EN, LED9END, LEDAEN, LEDAEND, LEDBEN, LEDBEND, LEDCEN, LEDCEND,
       LEDCS, LEDDEN, LEDDEND, LEDEEN, LEDEEND, LEDFEND, LEDRE, multiplexer_17_out, multiplexer_18_out, RWE,
       TTYCS;
  wire [14:0] DATAL0, DATAL1, DATAL2, DATAL3, DATAL4, DATAL5, DATAL6, DATAL7, DATAL8, DATAL9, DATALA, DATALB,
       DATALC, DATALD, DATALE, LEDDATA;
  wire [14:8] KBDATA15;

  assign CPUDATAOUT = KBRD ? {KBDATA15, DATA7, KBDATA} : 15'bz;  // Controlled_Buffer controlled_buffer_1
  assign CPUDATAOUT = LEDRE ? LEDDATA : 15'bz;  // Controlled_Buffer controlled_buffer_2
  assign CPUDATAOUT = IVECTRE ? IVECT : 15'bz;  // Controlled_Buffer controlled_buffer_3
  Register #(.width(15)) register_1 (.D(DATAL0), .en(LED0EN), .Q(LED0), .clk(CLK));  // open: clr
  Register #(.width(15)) register_2 (.D(DATAL1), .en(LED1EN), .Q(LED1), .clk(CLK));  // open: clr
  Register #(.width(15)) register_3 (.D(DATAL2), .en(LED2EN), .Q(LED2), .clk(CLK));  // open: clr
  Register #(.width(15)) register_4 (.D(DATAL3), .en(LED3EN), .Q(LED3), .clk(CLK));  // open: clr
  Register #(.width(15)) register_5 (.D(DATAL4), .en(LED4EN), .Q(LED4), .clk(CLK));  // open: clr
  and and_1 (and_1_out, WE, LEDCS);
  Decoder #(.select(4)) decoder_1 (
    .out0(LED0END), .out1(LED1END), .out2(LED2END), .out3(LED3END), .out4(LED4END), .out5(LED5END),
    .out6(LED6END), .out7(LED7END), .out8(LED8END), .out9(LED9END), .out10(LEDAEND), .out11(LEDBEND),
    .out12(LEDCEND), .out13(LEDDEND), .out14(LEDEEND), .out15(LEDFEND), .sel(ADDR[3:0]), .en(and_1_out));
  Register #(.width(15)) register_6 (.D(DATAL5), .en(LED5EN), .Q(LED5), .clk(CLK));  // open: clr
  Register #(.width(15)) register_7 (.D(DATAL6), .en(LED6EN), .Q(LED6), .clk(CLK));  // open: clr
  Register #(.width(15)) register_8 (.D(DATAL7), .en(LED7EN), .Q(LED7), .clk(CLK));  // open: clr
  Register #(.width(15)) register_9 (.D(DATAL8), .en(LED8EN), .Q(LED8), .clk(CLK));  // open: clr
  Register #(.width(15)) register_10 (.D(DATAL9), .en(LED9EN), .Q(LED9), .clk(CLK));  // open: clr
  or or_1 (LED0EN, LED0END, LEDFEND);
  or or_2 (LED1EN, LED1END, LEDFEND);
  or or_3 (LED2EN, LED2END, LEDFEND);
  or or_4 (LED3EN, LED3END, LEDFEND);
  or or_5 (LED4EN, LED4END, LEDFEND);
  or or_6 (LED5EN, LED5END, LEDFEND);
  or or_7 (LED6EN, LED6END, LEDFEND);
  or or_8 (LED7EN, LED7END, LEDFEND);
  or or_9 (LED8EN, LED8END, LEDFEND);
  or or_10 (LED9EN, LED9END, LEDFEND);
  or or_11 (LEDAEN, LEDAEND, LEDFEND);
  or or_12 (LEDBEN, LEDBEND, LEDFEND);
  or or_13 (LEDCEN, LEDCEND, LEDFEND);
  or or_14 (LEDDEN, LEDDEND, LEDFEND);
  or or_15 (LEDEEN, LEDEEND, LEDFEND);
  Pull_Resistor pull_resistor_1 (.node(KBDATA15[14]));
  Pull_Resistor pull_resistor_2 (.node(KBDATA15[13]));
  Pull_Resistor pull_resistor_3 (.node(KBDATA15[12]));
  Pull_Resistor pull_resistor_4 (.node(KBDATA15[11]));
  Pull_Resistor pull_resistor_5 (.node(KBDATA15[10]));
  Pull_Resistor pull_resistor_6 (.node(KBDATA15[9]));
  Pull_Resistor pull_resistor_7 (.node(KBDATA15[8]));
  Pull_Resistor pull_resistor_8 (.node(DATA7));
  Register #(.width(15)) register_11 (.D(DATALA), .en(LEDAEN), .Q(LEDA), .clk(CLK));  // open: clr
  Register #(.width(15)) register_12 (.D(DATALB), .en(LEDBEN), .Q(LEDB), .clk(CLK));  // open: clr
  Register #(.width(15)) register_13 (.D(DATALC), .en(LEDCEN), .Q(LEDC), .clk(CLK));  // open: clr
  Register #(.width(15)) register_14 (.D(DATALD), .en(LEDDEN), .Q(LEDD), .clk(CLK));  // open: clr
  Register #(.width(15)) register_15 (.D(DATALE), .en(LEDEEN), .Q(LEDE), .clk(CLK));  // open: clr
  Multiplexer #(.width(15)) multiplexer_1 (.in0(CPUDATAIN), .in1(LED1), .out(DATAL0), .sel(LEDFEND));
  Multiplexer #(.width(15)) multiplexer_2 (.in0(CPUDATAIN), .in1(LED2), .out(DATAL1), .sel(LEDFEND));
  Multiplexer #(.width(15)) multiplexer_3 (.in0(CPUDATAIN), .in1(LED3), .out(DATAL2), .sel(LEDFEND));
  Multiplexer #(.width(15)) multiplexer_4 (.in0(CPUDATAIN), .in1(LED4), .out(DATAL3), .sel(LEDFEND));
  Multiplexer #(.width(15)) multiplexer_5 (.in0(CPUDATAIN), .in1(LED5), .out(DATAL4), .sel(LEDFEND));
  Multiplexer #(.select(4), .width(15)) multiplexer_6 (
    .in0(LED0), .in1(LED1), .in2(LED2), .in3(LED3), .in4(LED4), .in5(LED5), .in6(LED6), .in7(LED7),
    .in8(LED8), .in9(LED9), .in10(LEDA), .in11(LEDB), .in12(LEDC), .in13(LEDD), .in14(LEDE),
    .in15({15{1'b0}}), .out(LEDDATA), .sel(ADDR[3:0]));
  Multiplexer #(.width(15)) multiplexer_7 (.in0(CPUDATAIN), .in1(LED6), .out(DATAL5), .sel(LEDFEND));
  Multiplexer #(.width(15)) multiplexer_8 (.in0(CPUDATAIN), .in1(LED7), .out(DATAL6), .sel(LEDFEND));
  Multiplexer #(.width(15)) multiplexer_9 (.in0(CPUDATAIN), .in1(LED8), .out(DATAL7), .sel(LEDFEND));
  Multiplexer #(.width(15)) multiplexer_10 (.in0(CPUDATAIN), .in1(LED9), .out(DATAL8), .sel(LEDFEND));
  Multiplexer #(.width(15)) multiplexer_11 (.in0(CPUDATAIN), .in1(LEDA), .out(DATAL9), .sel(LEDFEND));
  and and_2 (LEDRE, RE, LEDCS);
  Multiplexer #(.width(15)) multiplexer_12 (.in0(CPUDATAIN), .in1(LEDB), .out(DATALA), .sel(LEDFEND));
  Multiplexer #(.width(15)) multiplexer_13 (.in0(CPUDATAIN), .in1(LEDC), .out(DATALB), .sel(LEDFEND));
  Multiplexer #(.width(15)) multiplexer_14 (.in0(CPUDATAIN), .in1(LEDD), .out(DATALC), .sel(LEDFEND));
  Multiplexer #(.width(15)) multiplexer_15 (.in0(CPUDATAIN), .in1(LEDE), .out(DATALD), .sel(LEDFEND));
  Multiplexer #(.width(15)) multiplexer_16 (.in0(CPUDATAIN), .in1(CPUDATAIN), .out(DATALE), .sel(LEDFEND));
  and and_3 (IOCS, ADDR[5], ADDR[6], ADDR[7], ADDR[8], ADDR[9], ADDR[10], ADDR[11], ADDR[12], ADDR[13], ADDR[14], 1'b1);
  and and_4 (TTYCS, IOCS, ADDR[0], ~ADDR[1], ~ADDR[2], ~ADDR[3], ADDR[4]);  // AND_Gate
  and and_5 (KBCS, IOCS, ~ADDR[0], ~ADDR[1], ~ADDR[2], ~ADDR[3], ADDR[4]);  // AND_Gate
  and and_6 (IVECTADDR, ADDR[0], ADDR[1], ADDR[2], ADDR[3], ADDR[4], ADDR[5], ADDR[6], ADDR[7], ADDR[8], ADDR[9], ADDR[10], ADDR[11], ADDR[12], ADDR[13], ADDR[14]);
  and and_7 (TTYWR, TTYCS, WE);
  and and_8 (and_8_out, TTYWR, DATA7);
  and and_9 (KBRD, KBCS, RE);
  and and_10 (and_10_out, KBCS, WE);
  Multiplexer multiplexer_17 (.in0(and_10_out), .in1(1'b0), .out(multiplexer_17_out), .sel(KBCLR));
  and and_11 (LEDCS, IOCS, ~ADDR[4], RWE);  // AND_Gate
  and and_12 (IVECTEN, IVECTADDR, WE);
  and and_13 (IVECTRE, IVECTADDR, RE);
  or or_16 (RWE, RE, WE);
  and and_14 (MEMCS, ~IOCS, RWE);  // AND_Gate
  Multiplexer multiplexer_18 (.in0(and_8_out), .in1(1'b0), .out(multiplexer_18_out), .sel(TTYCLR));
  D_Flip_Flop d_ff_1 (.clk(CLK), .D(multiplexer_17_out), .Q(KBCLR));  // open: Qn, preset, reset
  Register #(.width(15)) register_16 (.D(CPUDATAIN), .en(IVECTEN), .Q(IVECT), .clk(CLK));  // open: clr
  D_Flip_Flop d_ff_2 (.clk(CLK), .D(multiplexer_18_out), .Q(TTYCLR));  // open: Qn, preset, reset

  assign IRQ = KBIRQ;
  assign TTYDATA = CPUDATAIN[6:0];

  // Other names for the same wires on the sheet: DATA[14:0] = CPUDATAIN; KBDATA15[7:0] = {DATA7, KBDATA}
endmodule

module ADDER15 (
  input  [14:0] A,
  input  [14:0] B,
  input  CIN,
  output COUT,
  output [14:0] S
);

  wire and_16_out, and_17_out, and_18_out, and_19_out, and_20_out, and_21_out, and_22_out, and_23_out,
       and_24_out, and_25_out, and_26_out, and_27_out, and_28_out, and_29_out, and_30_out, and_31_out,
       and_32_out, and_33_out, and_34_out, and_35_out, and_36_out, and_37_out, and_38_out, and_39_out,
       and_40_out, and_41_out, and_42_out, and_43_out, and_44_out, and_45_out, and_46_out, and_47_out,
       and_48_out, C1F, C1L, C1M, C2F, C2L, C2M, C3F, C3L, C3M, C4F, C4L, C4M, C5F, C5M, G0F, G0L, G0M, G1F,
       G1L, G1M, G2F, G2L, G2M, G3F, G3L, G3M, G4F, G4L, G4M, P0F, P0L, P0M, P1F, P1L, P1M, P2F, P2L, P2M,
       P3F, P3L, P3M, P4F, P4L, P4M;

  xor xor_1 (G0F, A[0], B[0]);
  and and_1 (P0F, A[0], B[0]);
  xor xor_2 (G1F, A[1], B[1]);
  and and_2 (P1F, A[1], B[1]);
  xor xor_3 (G2F, A[2], B[2]);
  and and_3 (P2F, A[2], B[2]);
  xor xor_4 (G3F, A[3], B[3]);
  and and_4 (P3F, A[3], B[3]);
  xor xor_5 (G4F, A[4], B[4]);
  and and_5 (P4F, A[4], B[4]);
  xor xor_6 (G0M, A[5], B[5]);
  and and_6 (P0M, A[5], B[5]);
  xor xor_7 (G1M, A[6], B[6]);
  and and_7 (P1M, A[6], B[6]);
  xor xor_8 (G2M, A[7], B[7]);
  and and_8 (P2M, A[7], B[7]);
  xor xor_9 (G3M, A[8], B[8]);
  and and_9 (P3M, A[8], B[8]);
  xor xor_10 (G4M, A[9], B[9]);
  and and_10 (P4M, A[9], B[9]);
  xor xor_11 (G0L, A[10], B[10]);
  and and_11 (P0L, A[10], B[10]);
  xor xor_12 (G1L, A[11], B[11]);
  and and_12 (P1L, A[11], B[11]);
  xor xor_13 (G2L, A[12], B[12]);
  and and_13 (P2L, A[12], B[12]);
  xor xor_14 (G3L, A[13], B[13]);
  and and_14 (P3L, A[13], B[13]);
  xor xor_15 (G4L, A[14], B[14]);
  and and_15 (P4L, A[14], B[14]);
  and and_16 (and_16_out, P4L, C4L);
  and and_17 (and_17_out, P4F, C4F);
  and and_18 (and_18_out, P4M, C4M);
  and and_19 (and_19_out, P0F, CIN);
  and and_20 (and_20_out, P1F, G0F);
  and and_21 (and_21_out, CIN, P0F, P1F);
  and and_22 (and_22_out, P2F, G1F);
  and and_23 (and_23_out, P2F, P1F, G0F);
  and and_24 (and_24_out, P2F, P1F, P0F, CIN);
  and and_25 (and_25_out, P0M, C5F);
  and and_26 (and_26_out, P1M, G0M);
  and and_27 (and_27_out, C5F, P0M, P1M);
  and and_28 (and_28_out, P2M, G1M);
  and and_29 (and_29_out, P2M, P1M, G0M);
  and and_30 (and_30_out, P2M, P1M, P0M, C5F);
  and and_31 (and_31_out, P3M, G2M);
  and and_32 (and_32_out, P3M, P2M, G1M);
  and and_33 (and_33_out, P3M, P2M, P1M, G0M);
  and and_34 (and_34_out, P3M, P2M, P1M, P0M, C5F);
  or u_C5M (C5M, and_18_out, G4M);
  and and_35 (and_35_out, P0L, C5M);
  and and_36 (and_36_out, P1L, G0L);
  and and_37 (and_37_out, C5M, P0L, P1L);
  and and_38 (and_38_out, P2L, G1L);
  and and_39 (and_39_out, P2L, P1L, G0L);
  and and_40 (and_40_out, P2L, P1L, P0L, C5M);
  and and_41 (and_41_out, P3L, G2L);
  and and_42 (and_42_out, P3L, P2L, G1L);
  and and_43 (and_43_out, P3L, P2L, P1L, G0L);
  and and_44 (and_44_out, P3L, P2L, P1L, P0L, C5M);
  or C5L (COUT, and_16_out, G4L);
  and and_45 (and_45_out, P3F, G2F);
  and and_46 (and_46_out, P3F, P2F, G1F);
  and and_47 (and_47_out, P3F, P2F, P1F, G0F);
  and and_48 (and_48_out, P3F, P2F, P1F, P0F, CIN);
  or u_C5F (C5F, and_17_out, G4F);
  or u_C1F (C1F, G0F, and_19_out);
  or u_C2F (C2F, G1F, and_20_out, and_21_out);
  or u_C3F (C3F, G2F, and_22_out, and_23_out, and_24_out);
  or u_C4F (C4F, G3F, and_45_out, and_46_out, and_47_out, and_48_out);
  or u_C1M (C1M, G0M, and_25_out);
  or u_C2M (C2M, G1M, and_26_out, and_27_out);
  or u_C3M (C3M, G2M, and_28_out, and_29_out, and_30_out);
  or u_C4M (C4M, G3M, and_31_out, and_32_out, and_33_out, and_34_out);
  or u_C1L (C1L, G0L, and_35_out);
  or u_C2L (C2L, G1L, and_36_out, and_37_out);
  or u_C3L (C3L, G2L, and_38_out, and_39_out, and_40_out);
  or u_C4L (C4L, G3L, and_41_out, and_42_out, and_43_out, and_44_out);
  xor S4F (S[4], P4F, C4F);
  xor S3F (S[3], P3F, C3F);
  xor S2F (S[2], P2F, C2F);
  xor S1F (S[1], P1F, C1F);
  xor S0F (S[0], P0F, CIN);
  xor S4M (S[9], P4M, C4M);
  xor S3M (S[8], P3M, C3M);
  xor S2M (S[7], P2M, C2M);
  xor S1M (S[6], P1M, C1M);
  xor S0M (S[5], P0M, C5F);
  xor S4L (S[14], P4L, C4L);
  xor S3L (S[13], P3L, C3L);
  xor S2L (S[12], P2L, C2L);
  xor S1L (S[11], P1L, C1L);
  xor S0L (S[10], P0L, C5M);

  // Other names for the same wires on the sheet: First5A[4:0] = A[4:0]; Mid5A[4:0] = A[9:5]; Last5A[4:0] = A[14:10];
  //   First5B[4:0] = B[4:0]; Mid5B[4:0] = B[9:5]; Last5B[4:0] = B[14:10]; S0F = S[0]; S1F = S[1]; S2F = S[2];
  //   S3F = S[3]; S4F = S[4]; S0M = S[5]; S1M = S[6]; S2M = S[7]; S3M = S[8]; S4M = S[9]; S0L = S[10]; S1L = S[11];
  //   S2L = S[12]; S3L = S[13]; S4L = S[14]
endmodule

module REGS15 (
  input  [14:0] D,
  input  W,
  input  [2:0] SelD,
  input  CLK,
  input  [2:0] SelA,
  input  [2:0] SelB,
  output [14:0] R0,
  output [14:0] R1,
  output [14:0] R2,
  output [14:0] R3,
  output [14:0] R4,
  output [14:0] R5,
  output [14:0] R6,
  output [14:0] R7,
  output [14:0] A,
  output [14:0] B
);
endmodule

module ALU15 (
  input  [2:0] OP,
  input  CIN,
  input  [14:0] A,
  input  [14:0] B,
  input  OIN,
  output C,
  output O,
  output N,
  output Z,
  output [14:0] R
);

  wire and_2_out, and_3_out, and_4_out, and_5_out, and_6_out, and_7_out, and_8_out, and_9_out, and_10_out,
       and_11_out, and_12_out, and_13_out, and_14_out, and_15_out, and_16_out, and_17_out, and_18_out,
       and_19_out, and_20_out, and_21_out, and_22_out, and_23_out, and_24_out, and_25_out, and_26_out,
       and_27_out, and_28_out, and_29_out, and_30_out, and_31_out, and_32_out, and_33_out, and_34_out,
       and_35_out, and_36_out, and_37_out, and_38_out, and_39_out, and_40_out, and_41_out, and_42_out,
       and_43_out, and_44_out, and_45_out, and_46_out, and_47_out, and_48_out, and_49_out, and_50_out,
       and_51_out, and_52_out, and_53_out, and_54_out, and_55_out, and_56_out, and_57_out, and_58_out,
       and_59_out, and_60_out, and_61_out, not_2_out, not_3_out, not_4_out, not_5_out, not_6_out, not_7_out,
       not_8_out, not_9_out, not_10_out, not_11_out, not_12_out, not_13_out, not_14_out, not_15_out,
       not_16_out, not_17_out, not_18_out, not_19_out, not_20_out, not_21_out, not_22_out, not_23_out,
       not_24_out, not_25_out, not_26_out, not_27_out, not_28_out, not_29_out, not_30_out, not_31_out;
  wire [14:0] ADD, andGate, not_1_out, orGate, shiftLeftLogical, shiftRightArithmetic, shiftRightLogical,
       SUB, xorGate;

  assign andGate = B & A;  // AND_Gate and_1, 15 bits wide
  assign not_1_out = ~B;  // NOT_Gate not_1, 15 bits wide
  ADDER15 adder15_1 (.A(A), .B(B), .CIN(1'b0), .S(ADD));  // open: COUT
  ADDER15 adder15_2 (.A(A), .B(not_1_out), .CIN(1'b1), .S(SUB));  // open: COUT
  assign orGate = B | A;  // OR_Gate or_1, 15 bits wide
  not not_2 (not_2_out, 1'b0);
  not not_3 (not_3_out, 1'b0);
  not not_4 (not_4_out, 1'b0);
  not not_5 (not_5_out, 1'b0);
  not not_6 (not_6_out, 1'b0);
  not not_7 (not_7_out, 1'b0);
  not not_8 (not_8_out, 1'b0);
  not not_9 (not_9_out, 1'b0);
  not not_10 (not_10_out, 1'b0);
  not not_11 (not_11_out, 1'b0);
  assign xorGate = B ^ A;  // XOR_Gate xor_1, 15 bits wide
  and and_2 (and_2_out, 1'b0, CIN);
  and and_3 (and_3_out, not_2_out, A[0]);
  and and_4 (and_4_out, 1'b0, A[1]);
  and and_5 (and_5_out, not_3_out, A[2]);
  and and_6 (and_6_out, 1'b0, A[3]);
  and and_7 (and_7_out, not_4_out, A[4]);
  and and_8 (and_8_out, 1'b0, A[5]);
  and and_9 (and_9_out, not_5_out, A[6]);
  and and_10 (and_10_out, 1'b0, A[7]);
  not not_12 (not_12_out, 1'b0);
  and and_11 (and_11_out, not_12_out, A[8]);
  and and_12 (and_12_out, 1'b0, A[9]);
  and and_13 (and_13_out, not_6_out, A[10]);
  and and_14 (and_14_out, 1'b0, A[11]);
  and and_15 (and_15_out, not_7_out, A[12]);
  and and_16 (and_16_out, 1'b0, A[13]);
  and and_17 (and_17_out, not_8_out, A[14]);
  and and_18 (and_18_out, 1'b0, B[0]);
  and and_19 (and_19_out, not_9_out, B[1]);
  and and_20 (and_20_out, 1'b0, B[2]);
  and and_21 (and_21_out, not_10_out, B[3]);
  and and_22 (and_22_out, 1'b0, B[4]);
  and and_23 (and_23_out, not_11_out, B[5]);
  and and_24 (and_24_out, 1'b0, B[6]);
  not not_13 (not_13_out, 1'b0);
  and and_25 (and_25_out, not_13_out, B[7]);
  and and_26 (and_26_out, 1'b0, B[8]);
  not not_14 (not_14_out, 1'b0);
  and and_27 (and_27_out, not_14_out, B[9]);
  and and_28 (and_28_out, 1'b0, B[10]);
  not not_15 (not_15_out, 1'b0);
  and and_29 (and_29_out, not_15_out, B[11]);
  and and_30 (and_30_out, 1'b0, B[12]);
  not not_16 (not_16_out, 1'b0);
  and and_31 (and_31_out, not_16_out, B[13]);
  and and_32 (and_32_out, 1'b1, CIN);
  not not_17 (not_17_out, 1'b1);
  and and_33 (and_33_out, not_17_out, A[0]);
  and and_34 (and_34_out, 1'b1, A[1]);
  not not_18 (not_18_out, 1'b1);
  and and_35 (and_35_out, not_18_out, A[2]);
  and and_36 (and_36_out, 1'b1, A[3]);
  not not_19 (not_19_out, 1'b1);
  and and_37 (and_37_out, not_19_out, A[4]);
  and and_38 (and_38_out, 1'b1, A[5]);
  not not_20 (not_20_out, 1'b1);
  and and_39 (and_39_out, not_20_out, A[6]);
  and and_40 (and_40_out, 1'b1, A[7]);
  not not_21 (not_21_out, 1'b1);
  and and_41 (and_41_out, not_21_out, A[8]);
  and and_42 (and_42_out, 1'b1, A[9]);
  not not_22 (not_22_out, 1'b1);
  and and_43 (and_43_out, not_22_out, A[10]);
  and and_44 (and_44_out, 1'b1, A[11]);
  not not_23 (not_23_out, 1'b1);
  and and_45 (and_45_out, not_23_out, A[12]);
  and and_46 (and_46_out, 1'b1, A[13]);
  not not_24 (not_24_out, 1'b1);
  and and_47 (and_47_out, not_24_out, A[14]);
  and and_48 (and_48_out, 1'b1, B[0]);
  not not_25 (not_25_out, 1'b1);
  and and_49 (and_49_out, not_25_out, B[1]);
  and and_50 (and_50_out, 1'b1, B[2]);
  not not_26 (not_26_out, 1'b1);
  and and_51 (and_51_out, not_26_out, B[3]);
  and and_52 (and_52_out, 1'b1, B[4]);
  not not_27 (not_27_out, 1'b1);
  and and_53 (and_53_out, not_27_out, B[5]);
  and and_54 (and_54_out, 1'b1, B[6]);
  not not_28 (not_28_out, 1'b1);
  and and_55 (and_55_out, not_28_out, B[7]);
  and and_56 (and_56_out, 1'b1, B[8]);
  not not_29 (not_29_out, 1'b1);
  and and_57 (and_57_out, not_29_out, B[9]);
  and and_58 (and_58_out, 1'b1, B[10]);
  not not_30 (not_30_out, 1'b1);
  and and_59 (and_59_out, not_30_out, B[11]);
  and and_60 (and_60_out, 1'b1, B[12]);
  not not_31 (not_31_out, 1'b1);
  and and_61 (and_61_out, not_31_out, B[13]);
  Multiplexer #(.select(3), .width(15)) multiplexer_1 (
    .in0(ADD), .in1(SUB), .in2(andGate), .in3(orGate), .in4(xorGate), .in5(shiftLeftLogical),
    .in6(shiftRightLogical), .in7(shiftRightArithmetic), .sel(OP));  // open: out
  // OR_Gate or_2 has open pins: in0=and_18_out, in1=and_19_out, out=open
  // OR_Gate or_3 has open pins: in0=and_20_out, in1=and_21_out, out=open
  // OR_Gate or_4 has open pins: in0=and_22_out, in1=and_23_out, out=open
  // OR_Gate or_5 has open pins: in0=and_24_out, in1=and_25_out, out=open
  // OR_Gate or_6 has open pins: in0=and_26_out, in1=and_27_out, out=open
  // OR_Gate or_7 has open pins: in0=and_28_out, in1=and_29_out, out=open
  // OR_Gate or_8 has open pins: in0=and_30_out, in1=and_31_out, out=open
  // OR_Gate or_9 has open pins: in0=and_2_out, in1=and_3_out, out=open
  // OR_Gate or_10 has open pins: in0=and_4_out, in1=and_5_out, out=open
  // OR_Gate or_11 has open pins: in0=and_6_out, in1=and_7_out, out=open
  // OR_Gate or_12 has open pins: in0=and_8_out, in1=and_9_out, out=open
  // OR_Gate or_13 has open pins: in0=and_10_out, in1=and_11_out, out=open
  // OR_Gate or_14 has open pins: in0=and_12_out, in1=and_13_out, out=open
  // OR_Gate or_15 has open pins: in0=and_14_out, in1=and_15_out, out=open
  // OR_Gate or_16 has open pins: in0=and_16_out, in1=and_17_out, out=open
  // OR_Gate or_17 has open pins: in0=and_32_out, in1=and_33_out, out=open
  // OR_Gate or_18 has open pins: in0=and_34_out, in1=and_35_out, out=open
  // OR_Gate or_19 has open pins: in0=and_36_out, in1=and_37_out, out=open
  // OR_Gate or_20 has open pins: in0=and_38_out, in1=and_39_out, out=open
  // OR_Gate or_21 has open pins: in0=and_40_out, in1=and_41_out, out=open
  // OR_Gate or_22 has open pins: in0=and_42_out, in1=and_43_out, out=open
  // OR_Gate or_23 has open pins: in0=and_44_out, in1=and_45_out, out=open
  // OR_Gate or_24 has open pins: in0=and_46_out, in1=and_47_out, out=open
  // OR_Gate or_25 has open pins: in0=and_48_out, in1=and_49_out, out=open
  // OR_Gate or_26 has open pins: in0=and_50_out, in1=and_51_out, out=open
  // OR_Gate or_27 has open pins: in0=and_52_out, in1=and_53_out, out=open
  // OR_Gate or_28 has open pins: in0=and_54_out, in1=and_55_out, out=open
  // OR_Gate or_29 has open pins: in0=and_56_out, in1=and_57_out, out=open
  // OR_Gate or_30 has open pins: in0=and_58_out, in1=and_59_out, out=open
  // OR_Gate or_31 has open pins: in0=and_60_out, in1=and_61_out, out=open

  assign OIN = B[14];
endmodule

module FLAGS8 (
  input  IRQ,
  input  [7:0] NF,
  input  [7:0] WM,
  input  CLK,
  output [7:0] F
);
endmodule

module IMM15 (
  input  [14:0] INST,
  output [14:0] SEXT
);
endmodule

module DECODE15 (
  input  [4:0] OPCODE,
  output SWI,
  output STORE,
  output LOAD,
  output [1:0] ASEL,
  output [1:0] BSEL,
  output [2:0] ALUOP,
  output [2:0] REGDATASRC,
  output REGW,
  output [1:0] FLAGSRC,
  output [7:0] FLAGWM,
  output SRPW,
  output SRFW
);
endmodule
